# Fritzing sketch MotionPet_estagioB (saved by Fritzing 1.0.5)
breadboards: 2

parts:
  U1 = ESP32 DevKit 38 pinos (generico MotionPet)
  M1 = HC-SR04 Ultrasonic Distance Sensor
  R1 = Resistor [resistance=1000 package=THT]
  R2 = Resistor [resistance=1000 package=THT]
  R3 = Resistor [resistance=300 package=THT]

nets:
  N1: U1.IO5, M1.TRIG
  N2: U1.IO34, R1.Pin_1, R2.Pin_0
  N3: U1.GND#J2.14, M1.GND, R3.Pin_0
  5V: U1.5V, M1.VCC
  N4: M1.ECHO, R1.Pin_0
  N5: R2.Pin_1, R3.Pin_1

custom parts:
  ESP32 DevKit 38 pinos (generico MotionPet): Parte generica: pinagem tipo DevKitC V4, 0,9 pol entre fileiras. NAO e o modelo exato da sua placa.
