# Fritzing sketch MotionPet_estagioC (saved by Fritzing 1.0.5)
breadboards: 2

parts:
  U1 = ESP32 DevKit 38 pinos (generico MotionPet)
  M1 = HC-SR04 Ultrasonic Distance Sensor
  R1 = Resistor [resistance=1000 package=THT]
  R2 = Resistor [resistance=1000 package=THT]
  R3 = Resistor [resistance=300 package=THT]
  M2 = Modulo TCRT5000 (comparador LM393) 4 pinos
  P1 = Potenciometro rotativo 3 terminais

nets:
  GND: U1.GND#J3.7, M1.GND, R3.Pin_0, M2.GND, P1.END_B
  N1: U1.IO5, M1.TRIG
  3V3: U1.3V3, M2.VCC, P1.END_A
  N2: U1.VP, P1.WIPER
  N3: U1.IO34, R1.Pin_1, R2.Pin_0
  N4: U1.IO35, M2.DO
  5V: U1.5V, M1.VCC
  N5: M1.ECHO, R1.Pin_0
  N6: R2.Pin_1, R3.Pin_1

custom parts:
  ESP32 DevKit 38 pinos (generico MotionPet): Parte generica: pinagem tipo DevKitC V4, 0,9 pol entre fileiras. NAO e o modelo exato da sua placa.
  Modulo TCRT5000 (comparador LM393) 4 pinos: Parte generica: Modulo TCRT5000 (comparador LM393) 4 pinos. Ordem dos pinos: ['VCC', 'GND', 'DO', 'AO'].
  Potenciometro rotativo 3 terminais: Parte generica: Potenciometro rotativo 3 terminais. Ordem dos pinos: ['END_A', 'WIPER', 'END_B'].
