# Fritzing sketch MotionPet_estagioD (saved by Fritzing 1.0.5)
breadboards: 2

parts:
  U1 = ESP32 DevKit 38 pinos (generico MotionPet)
  M1 = HC-SR04 Ultrasonic Distance Sensor
  R1 = Resistor [resistance=1000 package=THT]
  R2 = Resistor [resistance=1000 package=THT]
  R3 = Resistor [resistance=300 package=THT]
  M2 = Modulo TCRT5000 (comparador LM393) 4 pinos
  P1 = Potenciometro rotativo 3 terminais
  M3 = LCD 2004A V1.1 20x4 (HD44780, 16 pinos)
  R4 = Resistor [resistance=1000 package=THT]
  R5 = Resistor [resistance=300 package=THT]

nets:
  N1: U1.IO23, M3.D6
  N2: U1.IO22, M3.D5
  N3: U1.IO21, M3.D4
  GND: U1.GND#J3.7, M1.GND, R3.Pin_0, M2.GND, P1.END_B, M3.VSS, M3.RW, M3.K, R4.Pin_0
  N4: U1.IO19, M3.RS
  N5: U1.IO18, M3.E
  N6: U1.IO5, M1.TRIG
  3V3: U1.3V3, M2.VCC, P1.END_A
  N7: U1.VP, P1.WIPER
  N8: U1.IO34, R1.Pin_1, R2.Pin_0
  N9: U1.IO35, M2.DO
  N10: U1.IO27, M3.D7
  5V: U1.5V, M1.VCC, M3.VDD, R5.Pin_1
  N11: M1.ECHO, R1.Pin_0
  N12: R2.Pin_1, R3.Pin_1
  N13: M3.V0, R4.Pin_1
  N14: M3.A, R5.Pin_0

custom parts:
  ESP32 DevKit 38 pinos (generico MotionPet): Parte generica: pinagem tipo DevKitC V4, 0,9 pol entre fileiras. NAO e o modelo exato da sua placa.
  Modulo TCRT5000 (comparador LM393) 4 pinos: Parte generica: Modulo TCRT5000 (comparador LM393) 4 pinos. Ordem dos pinos: ['VCC', 'GND', 'DO', 'AO'].
  Potenciometro rotativo 3 terminais: Parte generica: Potenciometro rotativo 3 terminais. Ordem dos pinos: ['END_A', 'WIPER', 'END_B'].
  LCD 2004A V1.1 20x4 (HD44780, 16 pinos): Parte generica: LCD 2004A V1.1 20x4 (HD44780, 16 pinos). Ordem dos pinos: ['VSS', 'VDD', 'V0', 'RS', 'RW', 'E', 'D0', 'D1', 'D2', 'D3', 'D4', 'D5', 'D6', 'D7', 'A', 'K'].
